// Logisim project 332_pipelined.circ as structural Verilog
// REG FILE
module Register_FIle (
  input  [9:0] Write_Data,
  input  [1:0] Write_Reg,
  input  Ven_EN,
  input  Clock,
  input  [1:0] Read_Reg1,
  input  [1:0] Read_Reg2,
  output [9:0] Read_Data1,
  output [9:0] Read_Data_2
);

  wire R1, R2, R3, R4;
  wire [9:0] Dout1, Dout2, Dout3, Dout4;

  Decoder #(.select(2)) decoder_1 (.out0(R1), .out1(R2), .out2(R4), .out3(R3), .sel(Write_Reg), .en(Ven_EN));
  Register #(.width(10)) u_R1 (.D(Write_Data), .en(R1), .Q(Dout1), .clk(Clock));  // open: clr
  Register #(.width(10)) u_R3 (.D(Write_Data), .en(R3), .Q(Dout3), .clk(Clock));  // open: clr
  Register #(.width(10)) u_R2 (.D(Write_Data), .en(R2), .Q(Dout2), .clk(Clock));  // open: clr
  Register #(.width(10)) u_R4 (.D(Write_Data), .en(R4), .Q(Dout4), .clk(Clock));  // open: clr
  Multiplexer #(.select(2), .width(10), .enable("false")) multiplexer_1 (
    .in0(Dout1), .in1(Dout2), .in2(Dout4), .in3(Dout3), .out(Read_Data1), .sel(Read_Reg1));
  Multiplexer #(.select(2), .width(10), .enable("false")) multiplexer_2 (
    .in0(Dout1), .in1(Dout2), .in2(Dout4), .in3(Dout3), .out(Read_Data_2), .sel(Read_Reg2));

  // Other names for the same wires on the sheet: clk = Clock; Din[9:0] = Write_Data; do1[9:0] = Read_Data1;
  //   do2[9:0] = Read_Data_2; en = Ven_EN; RD1[1:0] = Read_Reg1; RD2[1:0] = Read_Reg2; writeReg[1:0] = Write_Reg
endmodule

module ALU (
  input  Cout,
  input  [1:0] Select_Opperation,
  input  Cin,
  input  [9:0] RS,
  input  [9:0] RT,
  output [9:0] OUTPUT
);

  wire [9:0] Add, And, Or, Sub;

  assign And = RS & RT;  // AND_Gate and_1, 10 bits wide
  assign Or = RS | RT;  // OR_Gate or_1, 10 bits wide
  Adder #(.width(10)) adder_1 (.a(RS), .b(RT), .out(Add), .cin(Cin), .cout(Cout));
  Subtractor #(.width(10)) subtractor_1 (.a(RS), .b(RT), .out(Sub), .bin(Cin), .bout(Cout));
  Multiplexer #(.select(2), .width(10), .enable("false")) multiplexer_1 (
    .in0(And), .in1(Or), .in2(Add), .in3(Sub), .out(OUTPUT), .sel(Select_Opperation));

  // Other names for the same wires on the sheet: mIn[1:0] = Select_Opperation; Result[9:0] = OUTPUT; RSin[9:0] = RS;
  //   RTin[9:0] = RT
endmodule
